# Fritzing sketch AffoFly_Receiver (saved by Fritzing 0.9.3b)
stripboards: 1

parts:
  Part1 = Arduino Pro Mini (3.3V)  # not connected
  Part2 = NRF24L01+ Breakout Board  # not connected
  TRRS1 = Audio Jack (TRRS) 3.5mm [part_number="LUMBERG JEITA RC-5325A" package="RC-5325A [SMD]"]  # not connected
  J1 = male pin header, 3 pins [form="♂ (male)"]
  C5 = Capacitor Polarized [package=cpol-radial-10uf-25v]
  C7 = Ceramic Capacitor [capacitance="100 nF" package="0805 [SMD, multilayer]"]
  LED1 = smd LED [color="Red (633nm)" package="0603 [SMD]"]
  LED2 = smd LED [color="Green (560nm)" package="0603 [SMD]"]
  R3 = Resistor [tolerance=±5% resistance=220 package=THT]
  R4 = Resistor [tolerance=±5% resistance=220 package="0805 [SMD]"]
  J2 = female pin header, 4 pins [form="♀ (female)"]
  J3 = female pin header, 4 pins [form="♀ (female)"]
  J4 = female pin header, 12 pins [form="♀ (female)"]
  J5 = female pin header, 12 pins [form="♀ (female)"]

nets:
  N1: J1.pin1, J2.pin1, J2.pin2, J2.pin3, J2.pin4, J4.pin9
  N2: J1.pin2, LED2.cathode, J3.pin1, J3.pin2, J3.pin3, J3.pin4, J4.pin3
  N3: J1.pin3, C5.+, C5.-, J5.pin2, J5.pin6, J5.pin10
  N4: C7.0, C7.1, LED2.anode, J5.pin12
  N5: LED1.cathode, J5.pin11
  N6: LED1.anode, J4.pin11, J4.pin12
  N7: R3.Pin_0, R3.Pin_1, R4.Pin_0, J4.pin10, J5.pin1, J5.pin9
  N8: J4.pin1, J4.pin8
  N9: J4.pin2, J5.pin8
  N10: J4.pin4, J5.pin3, J5.pin5
  N11: J4.pin5, J4.pin7, J5.pin7
